# Fritzing sketch Praktikum Eldas dioda (saved by Fritzing 0.9.3b)
breadboards: 1

parts:
  R1 = Resistor [tolerance=±5% resistance=1k package=THT]
  VCC1 = Battery block 9V
  LED1 = LED - 5mm [color="Red (633nm)" package="5 mm [THT]"]
  R2 = Resistor [tolerance=±5% resistance=1k package=THT]
  LED2 = LED - 5mm [color="Red (633nm)" package="5 mm [THT]"]

nets:
  N1: R1.Pin_0, VCC1.+
  N2: R1.Pin_1, LED1.anode, R2.Pin_0
  N3: VCC1.-, LED1.cathode, LED2.cathode
  N4: R2.Pin_1, LED2.anode
