# Fritzing sketch monitoring air dan kendali pompa (saved by Fritzing 0.9.3b)
breadboards: 1

parts:
  KY-1 = Keyes Relay [package=THT]
  U1 = HC-SR04 [chip_label=IC package="SIP (Single Inline) [THT]"]
  U2 = NodeMCU V3.0
  M1 = DC Motor
  PS1 = prefix0000 [part_number=S-350-60]
  JP1 = Header 2 [package=springterminal-2.54mm-2]

nets:
  N1: KY-1.signal, U2.D0
  VCC: KY-1.power, U1.Vcc, U2.3V3
  GND: KY-1.ground, U1.GND, U2.GND
  N2: KY-1.C, M1.pin_1
  N3: KY-1.NO, PS1.connector5
  N4: U1.Trig, U2.D1
  N5: U1.Echo, U2.D2
  N6: M1.pin_2, PS1.connector2
  N7: PS1.connector6, JP1.2
  N8: PS1.connector8, JP1.1

notes:
  Socket PLN
  Socket kabel pompa air 5V
  DC Power Supply

custom parts:
  Keyes Relay: The Keyes 5V relay module is suitable for SCM development, home appliance control. It uses a 5V~12V TIL control signal which can control DC / AC signal.
  HC-SR04: HC-SR04 ultrasound distance sensor
  NodeMCU V3.0: ESP8266 based NodeMCU
