# Fritzing sketch pot_led_buz (saved by Fritzing 0.9.3b)
breadboards: 1

parts:
  U1 = NodeMCU V3.0
  U2 = POT [package=pot_mammoth]
  LED1 = LED - 5mm [color="Red (633nm)" package="5 mm [THT]"]
  R1 = Resistor [tolerance=±5% resistance=220 package=THT]
  J1 = Piezo Speaker
  R2 = Resistor [tolerance=±5% resistance=220 package=THT]

nets:
  N1: U1.GND, U2.S, U2.E, LED1.cathode, J1.pin1
  N2: U1.D7, R2.Pin_1
  N3: U1.D8, R1.Pin_1
  N4: U1.A0, U2.A
  N5: LED1.anode, R1.Pin_0
  N6: J1.pin2, R2.Pin_0

notes:
  Search keyword:
  POT
  Search keyword:
  BUZ

custom parts:
  NodeMCU V3.0: ESP8266 based NodeMCU
