# Fritzing sketch praktikum eldas penurun tegangan (saved by Fritzing 0.9.3b)
breadboards: 1

parts:
  V1 = DC Power [voltage=9]
  IC1 = Voltage Regulator [package=to-220-alt]
  R1 = Resistor [tolerance=±5% resistance=220 package=THT]
  C1 = Capacitor Polarized [package=cpol-radial-1000uf-25v]
  C2 = Capacitor Polarized [package=cpol-radial-1000uf-25v]

nets:
  N1: V1.V+, IC1.IN, C1.+
  N2: V1.V-, IC1.GND, R1.Pin_1, C1.-, C2.-
  N3: IC1.OUT, R1.Pin_0, C2.+
