# Fritzing sketch simulasi parkir (saved by Fritzing 0.9.3b)
breadboards: 1

parts:
  U1 = HC-SR04 [chip_label=IC package="SIP (Single Inline) [THT]"]
  U2 = NodeMCU V3.0
  J1 = Piezo Speaker
  SERVO1 = Tower Pro SG90 servo [part_number=101246]

nets:
  VCC: U1.Vcc, SERVO1.+5V
  N1: U1.Trig, U2.D1
  N2: U1.Echo, U2.D2
  GND: U1.GND, J1.pin1, SERVO1.GND
  N3: U2.D0, J1.pin2
  N4: U2.D8, SERVO1.Signal

custom parts:
  HC-SR04: HC-SR04 ultrasound distance sensor
  NodeMCU V3.0: ESP8266 based NodeMCU
  Tower Pro SG90 servo: Original file by John De Cristofaro http://www.adafruit.com/products/1449 Adafruit Feedback Servo (Small) Edited by: e-radionica.com 28/9/2015
