# Fritzing sketch thermometer digital nodemcu (saved by Fritzing 0.9.3b)
breadboards: 1

parts:
  DHT1 = DHT11 Humitidy and Temperature Sensor
  U1 = NodeMCU V3.0
  LCM1602_IIC1 = LCM1602 IIC [part_number="LCM1602 IIC" chip_label="LCM1602 IIC" package="DIP (Dual Inline) [THT]"]
  U2 = LCD-16X2 [package=lcd-16x2]

nets:
  VDD: DHT1.VDD, U1.3V3
  N1: DHT1.DATA, U1.D3
  GND: DHT1.GND, U1.GND, LCM1602_IIC1.GND
  N2: U1.D1, LCM1602_IIC1.SCL
  N3: U1.D2, LCM1602_IIC1.SDA
  N4: U1.VU, LCM1602_IIC1.VCC
  VSS: LCM1602_IIC1.VSS, U2.VSS
  VDD_2: LCM1602_IIC1.VDD, U2.VDD
  N5: LCM1602_IIC1.V0, U2.VO
  N6: LCM1602_IIC1.RS, U2.RS
  N7: LCM1602_IIC1.RW, U2.R_W
  N8: LCM1602_IIC1.E, U2.E
  N9: LCM1602_IIC1.D0, U2.DB0
  N10: LCM1602_IIC1.D1, U2.DB1
  N11: LCM1602_IIC1.D2, U2.DB2
  N12: LCM1602_IIC1.D3, U2.DB3
  N13: LCM1602_IIC1.D4, U2.DB4
  N14: LCM1602_IIC1.D5, U2.DB5
  N15: LCM1602_IIC1.D6, U2.DB6
  N16: LCM1602_IIC1.D7, U2.DB7
  N17: LCM1602_IIC1.A, U2.A
  N18: LCM1602_IIC1.K, U2.K

custom parts:
  DHT11 Humitidy and Temperature Sensor: DHT11 Humidity and Temperature Sensor
  NodeMCU V3.0: ESP8266 based NodeMCU
  LCM1602 IIC: I2C-Module to use a 1602 or 2004 LCD on with the wire.h libory Serial LCD Modul
