# Fritzing sketch ultrasonic_bot_telegram (saved by Fritzing 0.9.3b)
breadboards: 1

parts:
  U3 = HC-SR04 [chip_label=IC package="SIP (Single Inline) [THT]"]
  U4 = NodeMCU V3.0
  J1 = Piezo Speaker
  R1 = Resistor [tolerance=±5% resistance=220 package=THT]

nets:
  VCC: U3.Vcc, U4.3V3
  N1: U3.Trig, U4.D1
  N2: U3.Echo, U4.D2
  GND: U3.GND, U4.GND, J1.pin1
  N3: U4.D0, R1.Pin_0
  N4: J1.pin2, R1.Pin_1

custom parts:
  HC-SR04: HC-SR04 ultrasound distance sensor
  NodeMCU V3.0: ESP8266 based NodeMCU
