# Fritzing sketch wiring pre test mengenal skema rangkaian (saved by Fritzing 0.9.3b)
breadboards: 1

parts:
  BAT1 = BC9VPC [package=bc9vpc]
  R1 = Resistor [tolerance=±5% resistance=220 package=THT]
  R2 = Resistor [tolerance=±5% resistance=220 package=THT]
  R3 = Resistor [tolerance=±5% resistance=220 package=THT]
  LED1 = LED - 5mm [color="Red (633nm)" package="5 mm [THT]"]
  IC1 = Voltage Regulator [package=to220-igo]
  C1 = Capacitor Polarized [package=cpol-radial-100uf-25v]
  C2 = Capacitor Polarized [package=cpol-radial-100uf-25v]
  R4 = Resistor [tolerance=±5% resistance=220 package=THT]
  LED2 = LED - 5mm [color="Red (633nm)" package="5 mm [THT]"]

nets:
  N1: BAT1.V+, R1.Pin_0
  N2: BAT1.V-, R3.Pin_1, LED1.cathode, IC1.GND, C1.-, C2.-, LED2.cathode
  N3: R1.Pin_1, R2.Pin_0, LED1.anode
  N4: R2.Pin_1, IC1.IN, C1.+
  N5: R3.Pin_0, IC1.OUT, C2.+, R4.Pin_1
  N6: R4.Pin_0, LED2.anode
